# Fritzing sketch Schaltplan (saved by Fritzing 0.9.2b)
breadboards: 1

parts:
  MH-ET_LIVE_ESP32_DEVKIT1 = MH-ET LIVE ESP32 DEVKIT 38 pins
  RHT1 = Humidity and Temperature Sensor RHT03
  KY-1 = Keyes Relay [package=THT]
  WATER_PUMP1 = water pump/motor
  J1 = Basic Servo
  M1 = Adafruit Anemometer [package=THT]  # not connected
  R1 = Resistor [tolerance=±5% resistance=220 package=THT]

nets:
  3V3: MH-ET_LIVE_ESP32_DEVKIT1.3V3, RHT1.Vcc, KY-1.power
  N1: MH-ET_LIVE_ESP32_DEVKIT1.IO32, RHT1.Data-signal
  N2: MH-ET_LIVE_ESP32_DEVKIT1.IO26, KY-1.signal
  N3: MH-ET_LIVE_ESP32_DEVKIT1.IO27, J1.vcc
  N4: MH-ET_LIVE_ESP32_DEVKIT1.GND#58, RHT1.GND_2, KY-1.ground, KY-1.NC, J1.gnd
  N5: MH-ET_LIVE_ESP32_DEVKIT1.5V, WATER_PUMP1.pin_2, J1.pulse
  N6: MH-ET_LIVE_ESP32_DEVKIT1.GND#64, R1.Pin_1
  N7: MH-ET_LIVE_ESP32_DEVKIT1.IO21, R1.Pin_0
  N8: KY-1.C, WATER_PUMP1.pin_1

notes:
  CO2Sensor

custom parts:
  MH-ET LIVE ESP32 DEVKIT 38 pins: http://mh.nodebb.com/topic/2/mh-et-live-esp32-devkit
  Keyes Relay: The Keyes 5V relay module is suitable for SCM development, home appliance control. It uses a 5V~12V TIL control signal which can control DC / AC signal.
  water pump/motor: WATER PUMP BY ARDUBLOCKTR
  Adafruit Anemometer: Adafruit Anemometer Wind Speed Sensor w/Analog Voltage Output.
